# Fritzing sketch Tacitus C0 (saved by Fritzing 0.8.7b)
breadboards: 1

parts:
  U1 = ATmega328 [package=tqfp]
  Y1 = Resonator [frequency="16 Mhz" package=THT]
  LED1 = smd LED [color="Green (570nm)" package="0805 [SMD]"]  # not connected
  C1 = Ceramic Capacitor [capacitance=100nF package="0805 [SMD, multilayer]"]  # not connected
  Q1 = MOSFET-NCHANNEL [package=sot23-3]  # not connected
  V1 = DC Power [voltage=5]
  C2 = Ceramic Capacitor [capacitance=10µF voltage=10V package="0805 [SMD, multilayer]"]
  C3 = Ceramic Capacitor [capacitance=10µF voltage=10V package="0805 [SMD, multilayer]"]
  U2 = Voltage Regulator LDO [package=sot23-5]

nets:
  GND: U1.GND, U1.AGND, Y1.GND, V1.V-, C2.0, C3.0, U2.GND
  N1: U1.VCC, U1.AVCC, U1.AREF, C3.1, U2.OUT
  N2: U1.PB6(XTAL1_TOSC1), Y1.0
  N3: U1.PB7(XTAL2_TOSC2), Y1.pin_1
  N4: V1.V+, C2.1, U2.IN, U2.EN
