# Fritzing sketch bareduino (saved by Fritzing 0.8.7b)
circuit board: 2.4cm x 3.5cm
breadboards: 1

parts:
  TO_XTAL = female pin header, 2 pins [form="♀ (female)"]
  J1 = AVR ISP 6 Pin [package=2x3_offset]
  U1 = ATmega328 [package=tqfp]

nets:
  N1: TO_XTAL.pin1, U1.PB7(XTAL2_TOSC2)
  N2: TO_XTAL.pin2, U1.PB6(XTAL1_TOSC1)
  N3: J1.1, U1.PB4(MISO)
  N4: J1.2, U1.VCC
  N5: J1.3, U1.PB5(SCK)
  N6: J1.4, U1.PB3(MOSI_OC2)
  N7: J1.5, U1.PC6(_RESET)
  GND: J1.6, U1.GND
